// Logisim project circuitos.circ as structural Verilog: 7 circuits, main circuit main
module main (
);

  validator validator_1 ();  // open: IN_01, in_3, CAN_WRITE__W, DUPLICATE__D, OUT_01, out_6
  _7_to_9_router u_7_to_9_router_1 ();  // open: _0, _1, _2, _3, _4, _5, _6, _7, _0_2, _1_2, _2_2, _3_2, _4_2, _5_2, _6_2, out_16, _7_2, out_18, _8, out_20, _9, out_22

  // Notes on the sheet:
  //   COORDINATOR
endmodule

module _7_to_9_router (
  input  _0,
  input  _1,
  input  _2,
  input  _3,
  input  _4,
  input  _5,
  input  _6,
  input  _7,
  output _0_2,
  output _1_2,
  output _2_2,
  output _3_2,
  output _4_2,
  output _5_2,
  output _6_2,
  output out_16,
  output _7_2,
  output out_18,
  output _8,
  output out_20,
  output _9,
  output out_22
);

  wire undriven;

  or or_1 (_0_2, _0, _0, _0, _0);
  or or_2 (_2_2, _1, _6, undriven);
  or or_3 (_3_2, undriven, _2, _2, _2, _2);
  or or_4 (_5_2, _3, _4, _4);

  assign _1_2 = _0;
  assign _4_2 = _2;
  assign _5 = _0;
  assign _6_2 = _4;
  assign _7 = _2;
  assign _7_2 = _0;
  assign _8 = _6;
  assign _9 = _2;
  assign out_16 = _4;
  assign out_18 = _0;
  assign out_20 = _6;
  assign out_22 = _2;
endmodule

module _2_bit_comparator (
  input  in_1,
  input  in_2,
  input  in_3,
  input  in_4,
  output out_5
);

  wire xnor_1_out, xnor_2_out;

  NotExactlyOne xnor_1 (.out(xnor_1_out), .in0(in_1), .in1(in_1), .in3(in_2), .in4(in_2));
  and and_1 (out_5, xnor_1_out, xnor_2_out);
  NotExactlyOne xnor_2 (.out(xnor_2_out), .in0(in_2), .in1(in_2), .in2(in_2), .in3(in_2), .in4(in_2));

  assign in_3 = in_2;
  assign in_4 = in_2;
endmodule

module _2_bit_memory (
  input  in_1,
  input  in_2,
  input  in_3,
  output out_4,
  output out_5
);

  // D_Flip_Flop d_ff_1: pin names not known; wires that end beside it: in_3, in_1, out_4
  // D_Flip_Flop d_ff_2: pin names not known; wires that end beside it: in_3, in_2, out_5
endmodule

module toggle (
  input  in_1,
  output out_2
);

  wire d_ff_1_p1, d_ff_1_p3;

  // D_Flip_Flop d_ff_1: pin names not known; wires that end beside it: d_ff_1_p1, 1'b1, d_ff_1_p3
  xor xor_1 (d_ff_1_p1, in_1, d_ff_1_p3);
  // NOT_Gate not_1 has open pins: in=d_ff_1_p1, out=open
  T_Flip_Flop t_ff_1 (.Q(out_2));  // open: clk, T, Qn, preset, reset, en
endmodule

module validator (
  input  CAN_WRITE__W,
  input  IN_01,
  input  in_3,
  output DUPLICATE__D,
  output OUT_01,
  output out_6
);

  wire and_1_out, and_2_out, not_1_out, undriven;

  _2_bit_comparator u_2_bit_comparator_1 (.in_1(IN_01), .in_3(in_3), .out_5(DUPLICATE__D), .in_2(OUT_01), .in_4(out_6));
  and and_1 (and_1_out, CAN_WRITE__W, IN_01, undriven);
  and and_2 (and_2_out, undriven, CAN_WRITE__W, in_3);
  // NOT_Gate not_1 has open pins: in=open, out=not_1_out
  // NOT_Gate not_2 has open pins: in=CAN_WRITE__W, out=open
  _2_bit_memory u_2_bit_memory_1 (.in_1(and_1_out), .in_2(and_2_out), .in_3(not_1_out), .out_4(OUT_01), .out_5(out_6));

  // Notes on the sheet:
  //   $$$$$
endmodule

module semaforo_transito (
  input  [1:0] in_1,
  output out_2,
  output out_3,
  output out_4
);

  wire nor_1_out, nor_4_out, not_1_out, not_2_out, not_3_out;

  not not_1 (not_1_out, in_1[1]);
  nor nor_1 (nor_1_out, not_1_out, out_4);
  nor nor_2 (out_4, in_1[1], nor_1_out);
  not not_2 (not_2_out, in_1[0]);
  nor nor_3 (out_2, not_2_out, nor_4_out);
  nor nor_4 (nor_4_out, in_1[0], out_2);
  not not_3 (not_3_out, out_4);
  and and_1 (out_3, nor_4_out, not_3_out);
endmodule
