// Logisim project router.circ as structural Verilog: 5 circuits, main circuit main
module main (
  output _6,
  output out_2,
  output out_3,
  output _7,
  output _0,
  output _1,
  output _2,
  output _5,
  output _4,
  output _3,
  output _9,
  output out_12,
  output out_13,
  output _8
);


  // Notes on the sheet:
  //   North
endmodule

module Two_Bit_Comparator (
  input  in_1,
  input  in_2,
  input  in_3,
  input  in_4,
  output out_5
);

  wire xnor_1_out, xnor_2_out;

  xnor xnor_1 (xnor_1_out, in_1, in_2);
  and and_1 (out_5, xnor_1_out, xnor_2_out);
  xnor xnor_2 (xnor_2_out, in_3, in_4);
endmodule

module Toggle (
  input  in_1,
  output out_2
);

  wire d_ff_1_q, not_1_out, xor_1_out;

  D_Flip_Flop d_ff_1 (.clk(xor_1_out), .D(1'b1), .Q(d_ff_1_q));  // open: Qn, preset, reset
  xor xor_1 (xor_1_out, in_1, d_ff_1_q);
  T_Flip_Flop t_ff_1 (.clk(not_1_out), .T(1'b1), .Q(out_2));  // open: Qn, preset, reset
  not not_1 (not_1_out, xor_1_out);
endmodule

module Double_Memory (
  input  in_1,
  input  in_2,
  input  in_3,
  output out_4,
  output out_5
);

  D_Flip_Flop d_ff_1 (.clk(in_3), .D(in_1), .Q(out_4));  // open: Qn, preset, reset
  D_Flip_Flop d_ff_2 (.clk(in_3), .D(in_2), .Q(out_5));  // open: Qn, preset, reset
endmodule

module Single_Memory (
  input  in_1,
  input  in_2,
  output out_3
);

  D_Flip_Flop d_ff_1 (.clk(in_2), .D(in_1), .Q(out_3));  // open: Qn, preset, reset
endmodule
