// Logisim project validator.circ as structural Verilog: 5 circuits, main circuit main
module main (
  input  CAN_WRITE__W,
  input  IN_01,
  input  in_3,
  output DUPLICATE__D,
  output OUT_01,
  output out_6
);

  wire and_1_out, and_2_out, not_1_out, not_2_out;

  Two_Bit_Comparator two_bit_comparator_1 (
    .in_1(IN_01), .in_3(in_3), .out_5(DUPLICATE__D), .in_2(OUT_01), .in_4(out_6));
  and and_1 (and_1_out, CAN_WRITE__W, IN_01);
  and and_2 (and_2_out, CAN_WRITE__W, in_3);
  not not_1 (not_1_out, CAN_WRITE__W);
  not not_2 (not_2_out, not_1_out);
  Double_Memory double_memory_1 (.in_1(and_1_out), .in_2(and_2_out), .in_3(not_2_out), .out_4(OUT_01), .out_5(out_6));

  // Notes on the sheet:
  //   $$$$$
endmodule

module Two_Bit_Comparator (
  input  in_1,
  input  in_2,
  input  in_3,
  input  in_4,
  output out_5
);

  wire xnor_1_out, xnor_2_out;

  xnor xnor_1 (xnor_1_out, in_1, in_2);
  and and_1 (out_5, xnor_1_out, xnor_2_out);
  xnor xnor_2 (xnor_2_out, in_3, in_4);
endmodule

module Toggle (
  input  in_1,
  output out_2
);

  wire d_ff_1_q, not_1_out, xor_1_out;

  D_Flip_Flop d_ff_1 (.clk(xor_1_out), .D(1'b1), .Q(d_ff_1_q));  // open: Qn, preset, reset
  xor xor_1 (xor_1_out, in_1, d_ff_1_q);
  T_Flip_Flop t_ff_1 (.clk(not_1_out), .T(1'b1), .Q(out_2));  // open: Qn, preset, reset
  not not_1 (not_1_out, xor_1_out);
endmodule

module Double_Memory (
  input  in_1,
  input  in_2,
  input  in_3,
  output out_4,
  output out_5
);

  D_Flip_Flop d_ff_1 (.clk(in_3), .D(in_1), .Q(out_4));  // open: Qn, preset, reset
  D_Flip_Flop d_ff_2 (.clk(in_3), .D(in_2), .Q(out_5));  // open: Qn, preset, reset
endmodule

module Single_Memory (
  input  in_1,
  input  in_2,
  output out_3
);

  D_Flip_Flop d_ff_1 (.clk(in_2), .D(in_1), .Q(out_3));  // open: Qn, preset, reset
endmodule
