// Logisim project circuitos.circ as structural Verilog: 12 circuits, main circuit main
module main (
  input  WRITE,
  output DUPLICATE
);

  wire button_1_out, button_2_out, button_3_out, button_4_out, button_5_out, button_6_out, button_7_out,
       button_8_out, codificador_4_a_2_1__0_2, codificador_4_a_2_1__1_2, controlador_botones_1__0,
       controlador_botones_1__1, controlador_botones_1__2, controlador_botones_1__3, or_1_out, or_2_out,
       or_3_out, or_4_out;

  Button button_1 (.out(button_1_out));
  or or_1 (or_1_out, button_1_out, button_2_out);
  Button button_2 (.out(button_2_out));
  Button button_3 (.out(button_3_out));
  or or_2 (or_2_out, button_3_out, button_4_out);
  Button button_4 (.out(button_4_out));
  Button button_5 (.out(button_5_out));
  or or_3 (or_3_out, button_5_out, button_6_out);
  Button button_6 (.out(button_6_out));
  Button button_7 (.out(button_7_out));
  or or_4 (or_4_out, button_7_out, button_8_out);
  Button button_8 (.out(button_8_out));
  controlador_botones controlador_botones_1 (
    ._6(or_1_out), ._7(or_2_out), ._8(or_3_out), ._9(or_4_out), ._0(controlador_botones_1__0),
    ._1(controlador_botones_1__1), ._2(controlador_botones_1__2), ._3(controlador_botones_1__3));
  codificador_4_a_2 codificador_4_a_2_1 (
    ._0(controlador_botones_1__0), ._1(controlador_botones_1__1), ._2(controlador_botones_1__2),
    ._3(controlador_botones_1__3), ._0_2(codificador_4_a_2_1__0_2), ._1_2(codificador_4_a_2_1__1_2));
  validador validador_1 (
    .IN_01(codificador_4_a_2_1__0_2), .in_3(codificador_4_a_2_1__1_2), .WRITE__W(WRITE),
    .DUPLICATE__D(DUPLICATE));  // open: OUT_01, out_6
  enrutador_7_a_9 enrutador_7_a_9_1 ();  // open: _0, _1, _2, _3, _4, _5, _6, _7, _0_2, _1_2, _2_2, _3_2, _4_2, _5_2, _6_2, out_16, _7_2, out_18, _8, out_20, _9, out_22

  // Notes on the sheet:
  //   COORDINATOR
endmodule

module toggle (
  input  in_1,
  output out_2
);

  wire d_ff_1_q, not_1_out, xor_1_out;

  D_Flip_Flop #(.NewFFLayout("false")) d_ff_1 (.clk(xor_1_out), .D(1'b1), .Q(d_ff_1_q));  // open: Qn, preset, reset
  xor xor_1 (xor_1_out, in_1, d_ff_1_q);
  T_Flip_Flop #(.NewFFLayout("false")) t_ff_1 (.clk(not_1_out), .T(1'b1), .Q(out_2));  // open: Qn, preset, reset
  not not_1 (not_1_out, xor_1_out);
endmodule

module semaforo_transito (
  input  in_1,
  output Rojo,
  output Verde,
  output Amarillo
);

  wire not_1_out, not_2_out, not_3_out, rom_1_data;
  wire [1:0] counter_1_q, counter_2_q, counter_3_q;

  Counter #(.width(2), .max('h3), .ongoal("continue"), .behavior("old")) counter_1 (
    .count(in_1), .Q(counter_1_q), .clk(in_1), .clr(rom_1_data));  // open: load, D, carry, preset
  Counter #(.width(2), .max('h3), .ongoal("continue"), .behavior("old")) counter_2 (
    .count(in_1), .Q(counter_2_q), .clk(in_1), .clr(rom_1_data));  // open: load, D, carry, preset
  Counter #(.width(2), .max('h3), .ongoal("continue"), .behavior("old")) counter_3 (
    .count(in_1), .Q(counter_3_q), .clk(in_1), .clr(rom_1_data));  // open: load, D, carry, preset
  ROM #(.addrWidth(2), .dataWidth(1), .Select("high")) rom_1 (.addr(counter_1_q), .data(rom_1_data));
  ROM #(.addrWidth(2), .dataWidth(1), .Select("high")) rom_2 (.addr(counter_2_q), .data(Verde));
  ROM #(.addrWidth(2), .dataWidth(1), .Select("high")) rom_3 (.addr(counter_3_q), .data(Amarillo));
  not not_1 (not_1_out, rom_1_data);
  and and_1 (Rojo, not_1_out, not_2_out, not_3_out);
  not not_2 (not_2_out, Verde);
  not not_3 (not_3_out, Amarillo);

  // Notes on the sheet:
  //   Reinicio
  //   contents of rom_1 (hex, n*v repeats v):
  //   0 0 0 1
  //   contents of rom_2 (hex, n*v repeats v):
  //   0 1
  //   contents of rom_3 (hex, n*v repeats v):
  //   0 0 1
endmodule

module validador (
  input  WRITE__W,
  input  IN_01,
  input  in_3,
  output DUPLICATE__D,
  output OUT_01,
  output out_6
);

  wire and_1_out, and_2_out, Retraso_out_2;

  comparador_2_bits Comparador (.in_1(IN_01), .in_3(in_3), .out_5(DUPLICATE__D), .in_2(OUT_01), .in_4(out_6));
  and and_1 (and_1_out, WRITE__W, IN_01);
  and and_2 (and_2_out, WRITE__W, in_3);
  retraso Retraso (.in_1(WRITE__W), .out_2(Retraso_out_2));
  memoria_2_bits Memoria (.in_1(and_1_out), .in_2(and_2_out), .in_3(Retraso_out_2), .out_4(OUT_01), .out_5(out_6));

  // Notes on the sheet:
  //   $$$$$
endmodule

module retraso (
  input  in_1,
  output out_2
);

  wire not_2_out;

  not not_1 (out_2, not_2_out);
  not not_2 (not_2_out, in_1);
endmodule

module memoria_2_bits (
  input  in_1,
  input  in_2,
  input  in_3,
  output out_4,
  output out_5
);

  D_Flip_Flop #(.NewFFLayout("false")) d_ff_1 (.clk(in_3), .D(in_1), .Q(out_4));  // open: Qn, preset, reset
  D_Flip_Flop #(.NewFFLayout("false")) d_ff_2 (.clk(in_3), .D(in_2), .Q(out_5));  // open: Qn, preset, reset
endmodule

module comparador_2_bits (
  input  in_1,
  input  in_2,
  input  in_3,
  input  in_4,
  output out_5
);

  wire xnor_1_out, xnor_2_out;

  xnor xnor_1 (xnor_1_out, in_1, in_2);
  and and_1 (out_5, xnor_1_out, xnor_2_out);
  xnor xnor_2 (xnor_2_out, in_3, in_4);
endmodule

module enrutador_7_a_9 (
  input  _0,
  input  _1,
  input  _2,
  input  _3,
  input  _4,
  input  _5,
  input  _6,
  input  _7,
  output _0_2,
  output _1_2,
  output _2_2,
  output _3_2,
  output _4_2,
  output _5_2,
  output _6_2,
  output out_16,
  output _7_2,
  output out_18,
  output _8,
  output out_20,
  output _9,
  output out_22
);

  or or_1 (_0_2, _0, _5);
  or or_2 (_2_2, _1, _6);
  or or_3 (_3_2, _2, _7);
  or or_4 (_5_2, _3, _4);

  assign _1_2 = _0;
  assign _4_2 = _2;
  assign _6_2 = _4;
  assign _7_2 = _5;
  assign _8 = _6;
  assign _9 = _7;
  assign out_16 = _4;
  assign out_18 = _5;
  assign out_20 = _6;
  assign out_22 = _7;

  // Notes on the sheet:
  //   Fases
  //   Semáforos
endmodule

module controlador_botones (
  input  _6,
  input  _7,
  input  _8,
  input  _9,
  output _0,
  output _1,
  output _2,
  output _3
);

  wire or_1_out, or_2_out, or_3_out, or_4_out;

  or or_1 (or_1_out, _7, _8, _9);
  or or_2 (or_2_out, _6, _8, _9);
  or or_3 (or_3_out, _6, _7, _9);
  or or_4 (or_4_out, _6, _7, _8);
  switch switch_1 (.in_1(_6), .in_2(or_1_out), .out_3(_0));
  switch switch_2 (.in_1(_7), .in_2(or_2_out), .out_3(_1));
  switch switch_3 (.in_1(_8), .in_2(or_3_out), .out_3(_2));
  switch switch_4 (.in_1(_9), .in_2(or_4_out), .out_3(_3));
endmodule

module switch (
  input  in_1,
  input  in_2,
  output out_3
);

  wire or_1_out;

  or or_1 (or_1_out, in_1, in_2);
  D_Flip_Flop d_ff_1 (.clk(or_1_out), .Q(out_3), .preset(in_1), .reset(in_2));  // open: D, Qn
endmodule

module codificador_4_a_2 (
  input  _0,
  input  _1,
  input  _2,
  input  _3,
  output _0_2,
  output _1_2
);

  wire and_1_out, and_2_out, and_3_out;

  and and_1 (and_1_out, ~_0, ~_1, _2, ~_3);  // AND_Gate
  and and_2 (and_2_out, ~_0, ~_1, ~_2, _3);  // AND_Gate
  and and_3 (and_3_out, ~_0, _1, ~_2, ~_3);  // AND_Gate
  or or_1 (_0_2, and_1_out, and_2_out);
  or or_2 (_1_2, and_2_out, and_3_out);
endmodule

module decodificador_3_a_8 (
  input  _0,
  input  _1,
  input  _2,
  output _0_2,
  output _1_2,
  output _2_2,
  output _3,
  output _4,
  output _5,
  output _6,
  output _7
);

  and and_1 (_0_2, ~_2, ~_1, ~_0);  // AND_Gate
  and and_2 (_1_2, ~_2, ~_1, _0);  // AND_Gate
  and and_3 (_2_2, ~_2, _1, ~_0);  // AND_Gate
  and and_4 (_3, ~_2, _1, _0);  // AND_Gate
  and and_5 (_4, _2, ~_1, ~_0);  // AND_Gate
  and and_6 (_5, _2, ~_1, _0);  // AND_Gate
  and and_7 (_6, _2, _1, ~_0);  // AND_Gate
  and and_8 (_7, _2, _1, _0);
endmodule
